# Fritzing sketch pedalboard_neopixel.1.13 (saved by Fritzing 0.9.3b)
breadboards: 6

parts:
  U13 = 74HC4051 [package=so16]
  Atmega1284P1 = ATmega1284P [package=pdpi]
  XTAL1 = Crystal [frequency="16 Mhz" package=THT]
  C1 = Capacitor [part_number=22pf package=cap-pth-small2]
  R1 = Resistor [tolerance=±10% resistance=10k package="1206 [SMD]"]
  C2 = Capacitor [part_number=22pf package=cap-pth-small2]
  C4 = Ceramic Capacitor [capacitance=100nF voltage=16V package="100 mil [THT, multilayer]"]
  Componente1 = FTDI Basic Programmer
  M1 = RioRand LM2596
  Componente2 = PowerBoost 500 Charger  # not connected
  U14 = LIPO-2000mAh [package=lipo-2000]  # not connected
  U15 = SWITCH-SPST-2 [package=switch-spst-vertical]
  R2 = Resistor [tolerance=±10% resistance=10k package="1206 [SMD]"]
  Componente4 = Bluetooth HC-05 Macho
  R4 = Resistor [tolerance=±5% resistance=220 package="2010 [SMD]"]
  LED1 = smd LED [color="Red (633nm)" package="0603 [SMD]"]
  LED3 = smd LED [color="Red (633nm)" package="0603 [SMD]"]
  R6 = Resistor [tolerance=±5% resistance=220 package="2010 [SMD]"]
  Componente5 = Adafruit 1.3in 240x240 IPS TFT [part_number="oled 128x64  I2C  screen"]
  BUTTON1 = Arcade Button (blue)
  BUTTON2 = Arcade Button (blue)
  BUTTON3 = Arcade Button (blue)
  BUTTON4 = Arcade Button (blue)
  BUTTON5 = Arcade Button (blue)
  BUTTON6 = Arcade Button (blue)
  BUTTON7 = Arcade Button (green)
  BUTTON8 = Arcade Button (red)
  BUTTON9 = Arcade Button (pink)
  BUTTON10 = Arcade Button (green)
  NEOPIXEL1 = Neopixel Strip -- Black (30/m) [part_number=1376]
  NEOPIXEL2 = Neopixel Strip -- Black (30/m) [part_number=1376]
  NEOPIXEL3 = Neopixel Strip -- Black (30/m) [part_number=1376]
  NEOPIXEL4 = Neopixel Strip -- Black (30/m) [part_number=1376]
  NEOPIXEL5 = Neopixel Strip -- Black (30/m) [part_number=1376]
  Componente6 = Logic Level Converter [part_number="Logic level converter 3v/5v"]
  VCC1 = Battery
  R7 = Resistor [tolerance=±5% resistance=220 package="2010 [SMD]"]
  LED4 = smd LED [color="Red (633nm)" package="0603 [SMD]"]
  C3 = Capacitor Polarized [package=cpol-radial-10uf-25v]
  U16 = POT [package=alps_pot]
  U16_2 = POT [part_number="Joystck analogico NOT A POT!!" package=pot_alpha_rv16af-20]

nets:
  N1: U13.IO4, BUTTON2.no_name_yet#1
  N2: U13.IO6, BUTTON4.no_name_yet#1
  N3: U13.IO, Atmega1284P1.PC3
  N4: U13.IO7, BUTTON8.no_name_yet#1
  N5: U13.IO5, BUTTON6.no_name_yet#1
  VSS: U13.INH, U13.VEE, U13.VSS, Atmega1284P1.GND#10, C1.2, Componente4.GND, LED1.cathode, LED3.cathode, BUTTON1.no_name_yet#2, BUTTON2.no_name_yet#2, BUTTON3.no_name_yet#2, BUTTON4.no_name_yet#2, BUTTON5.no_name_yet#2, BUTTON6.no_name_yet#2, BUTTON7.no_name_yet#2, BUTTON8.no_name_yet#2, BUTTON9.no_name_yet#2, BUTTON10.no_name_yet#2
  N6: U13.C, Atmega1284P1.PC4
  N7: U13.B, Atmega1284P1.PC5
  N8: U13.A, Atmega1284P1.PC6
  N9: U13.IO3, BUTTON9.no_name_yet#1
  N10: U13.IO0, BUTTON1.no_name_yet#1
  N11: U13.IO1, BUTTON5.no_name_yet#1
  N12: U13.IO2, BUTTON3.no_name_yet#1
  N13: Atmega1284P1.PB2, Componente5.RESET
  N14: Atmega1284P1.PB3, Componente6.TX2_HV
  N15: Atmega1284P1.PB4, Componente6.RX2_HV
  N16: Atmega1284P1.PB5, Componente6.RX_HV
  N17: Atmega1284P1.PB6, Componente6.TX_HV
  N18: Atmega1284P1.RESET, R1.Pin_0, C4.1
  N19: Atmega1284P1.VCC, Atmega1284P1.AVCC, R1.Pin_1, Componente1.POWER, M1.Pin_3, NEOPIXEL1.+5V#3, Componente6.HV, C3.+, U16.A, U16_2.A
  N20: Atmega1284P1.XTAL2, XTAL1.pin_0, C2.2
  N21: Atmega1284P1.XTAL1, XTAL1.pin_1, C1.1
  N22: Atmega1284P1.PD0, Componente1.TXO
  N23: Atmega1284P1.PD1, Componente1.RXI, Componente4.TXD
  N24: Atmega1284P1.PD5, BUTTON10.no_name_yet#1
  N25: Atmega1284P1.PD6, BUTTON7.no_name_yet#1
  N26: Atmega1284P1.PD7, NEOPIXEL1.Din
  GND: Atmega1284P1.GND#30, C2.1, Componente1.GND, M1.Pin_4, Componente5.GND, NEOPIXEL1.GND#1, Componente6.GND, VCC1.-, LED4.cathode, C3.-, U16.E, U16_2.E
  N27: Atmega1284P1.PA2, R2.Pin_0
  N28: Atmega1284P1.PA0, U16.S, U16_2.S
  N29: C4.0, Componente1.DTR
  N30: M1.Pin_1, U15.P, R2.Pin_1
  N31: Componente4.State, R4.Pin_0
  N32: Componente4.VCC, R6.Pin_0
  N33: Componente5.VIN, Componente5.BACKLIGHT, Componente6.LV, VCC1.+, R7.Pin_0
  N34: Componente5.SCK, Componente6.TX_LV
  N35: Componente5.MOSI, Componente6.RX_LV
  N36: Componente5.TFTDC, Componente6.TX2_LV
  N37: Componente5.CARDCS, Componente6.RX2_LV
  N38: NEOPIXEL1.+5V#4, NEOPIXEL2.+5V#3
  N39: NEOPIXEL1.Dout, NEOPIXEL2.Din
  N40: NEOPIXEL1.GND#6, NEOPIXEL2.GND#1
  N41: NEOPIXEL2.+5V#4, NEOPIXEL3.+5V#3
  N42: NEOPIXEL2.Dout, NEOPIXEL3.Din
  N43: NEOPIXEL2.GND#6, NEOPIXEL3.GND#1
  N44: NEOPIXEL3.+5V#4, NEOPIXEL5.+5V#3
  N45: NEOPIXEL3.Dout, NEOPIXEL5.Din
  N46: NEOPIXEL3.GND#6, NEOPIXEL5.GND#1
  N47: NEOPIXEL4.GND, NEOPIXEL5.GND#6
  N48: NEOPIXEL4.Din, NEOPIXEL5.Dout
  N49: NEOPIXEL4.+5V, NEOPIXEL5.+5V#4

notes:
  Led de Estado conexion Bluetooth.
  Encendido cuando hay una conexion Bluetooth establecida.
  Resistencia 220 ohms.
  Conexion:GND/
  Pin STATE (HC-05)
  Modulo de conexión Bluetooth HC-05.
  SLAVE
  AT ROLE=0 (Slave)
  115200 BAUDIOS
  CMODE=1
  Hay que configurarlo mediante comandos en el monitor serie. Para que linkee con otro modulo master (hay que mirar las MAC del MASTER y el SLAVE para poder linkarlos)
  Conexión.VCC/GND/
  Pin TX (Atmel)
  Modulo de Bateria
  TP-4056.
  4 pines.
  Conexiónes.
  B+/B-= Bateria+/-.
  OUT+=Interruptor.
  OUT-=BoosterMT3608.
  Utlizar el puerto micro- usb para cargar la bateria
  Modulo Programación
  FTDI-USB.
  Conexión a traves del USB al PC para poder subir codigo al chip Atmel 1284.
  Posibilidad de posicionar el jumper 3,3/5 Voltios.
  3,3V para la configuración de los modulos HC-05.
  5V para subir codigo al chip.
  Con 5 pines de conexión
  VCC/GND/TX/RX y el pin DTR que lleva un condensador de 100 nf (azul) y se conecta al pin RESET (Atmel).
  (los pines tx y rx van al tx y rx del atmel)
  Cable morado que sale del IN+ del booster, pasa por Resistencia de 10kohms y va al pin A4 (Atmel)
  BOOSTER MT3608.
  Ajustar el tornillo hasta que baje de los 20voltios a los 5 voltios (realizar la lectura en OUT+ y OUT-)
  (Antes de conectar el circuito o el chip)
  Bateria 3-5 Voltios
  Alimenta todo el circuito y utiliza el TP-4056 para realizar la carga y pasa por el booster MT3608 para entregar un voltaje constante de 5v al circuito
  Interruptor ON/OFF
  Para apagar/encender el dispositivo.
  Led de encendido.
  Cuando el dispositivo este encendido
  ESTO NO ES UN POT EN REALIDAD!!!
  ES LA CONEXION A UN PEDAL DE EXPRESION VOLUME/WAH.
  En realidad no son baterias..
  Teneis que poner una fuente de alimentacion de 3 voltios, necesarios para el rectificador de voltaje y la pantalla ili 9341...
  Tambien hay otra opcion de rebajar los 5 voltios mediante resistencias...
  Fuente de 3V
  Pantalla ILI9341.
  Conectada al rectificador de voltaje y al chip atmel.
  Cable naranja PIN RESET(ATMEL)
  Cable amarillo PIN DC
  Cable cian PIN CS
  Cable azul PIN MOSI
  Cable gris PIN SCK.
  Alimentar los dos pines LED y VCC y el pin GND A UNA FUENTE DE ALIMENTACION DE 3 VOLTIOS!!
  Led de encendido.3V
  Cuando el dispositivo este encendido y la fuente de alimentación de 3v
  Cristal de cuarzo de 16 mhz necesario para el chip atmel 1284, lleva dos condensadores de 22 picofaradios conectados a GND
  R10KOhms PIN RESET (atmel)
  R 10Kohms para la lectura de la bateria al pin analogico del atmel]
  LEDSTRIP WS2812B 5V Conectada al pin 15 del chip atmel
  PEDAL/PRESET 1
  PEDAL/PRESET 2
  PEDAL/PRESET 3
  PEDAL/PRESET 4
  PEDAL/PRESET 5]
  PEDAL/PRESET 6
  led VOLUME.
  Encendido cuando hay actividad en VOLUME.
  Luz azul o roja cuando se activa el pedal de WAH/VOLUME
  Boton BAJAR BANCO DE PRESETS.
  Bajar VOLUME en modo PEDALES.
  UNDO en modo LOOPER.
  Boton SUBIR BANCO DE PRESETS.
  Subir VOLUME en modo PEDALES.
  REDO en modo LOOPER.
  Boton PEDALES.
  Entrar pantalla PEDALES.
  Mantener pulsado para afinador.
  Boton LOOPER.
  Entrar pantalla LOOPER.
  Mantener pulsado para MUTE.
  Rectificador de voltaje
  (CONVERTIDOR TTS BI-DIRECCIONAL LOGICO 4 CANALES 5V/3V )
  Pines HV/ GND conectados a 5V.
  Pines LV/GND conectados a 3V
  PINES H1-H4 conectados al chip atme.l
  H1=DC (PIN 3 atmel).
  H2=CS (PIN 4 atmel.)
  H3=MOSI (pin 5 atme).
  H4=SCK(pin 7 atmel).
  PINES L1-L4 conectados a la pantalla ILI934.
  L1=DC (ili9341l).
  L2=CS (ili9341l).
  L3=MOSI (ili934).
  L4=SCK (ili9341l).
  Chip Atmel 1284
  Condensador electrolitico 10 microfaradios
  LED MODO PEDALES ACTIVO
  LED MODO LOOPER ACTIVO

custom parts:
  ATmega1284P: AVR 8-bit microcontroller.
  Adafruit 1.3in 240x240 IPS TFT: We've been looking for a display like this for a long time - it's so small only 1.3" diagonal but has a high density 260 ppi, 240x240 pixel display with full-angle viewing. It looks a lot like our 1.44" 128x128 display, but has 4x as many pixels and looks great at any angle. We've seen displays of this caliber used in smartwatches and small electronic devices but they've always been MIPI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
  Arcade Button (blue): Adafruit Arcade Button (blue)
  Arcade Button (green): Adafruit Arcade Button (green)
  Arcade Button (red): Adafruit Arcade Button (red)
  Arcade Button (pink): Adafruit Arcade Button (pink)
  Neopixel Strip -- Black (30/m): These NeoPixel strips have 30 digitally-addressable pixel LEDs per meter and are very affordable and are only 12.5 mm wide, 10 mm if you remove the strip from the casing.
