# Fritzing sketch desktop_MIDI_controller_0.30_synaptic (saved by Fritzing 0.9.3b)
breadboards: 5

parts:
  U1 = POT [part_number="AMP76   POS.2 POT10KLINEAR" package=pot_alpha_rv16af-20]
  U2 = POT [part_number="AMP77  POS.3  POT10KLINEAR" package=pot_alpha_rv16af-20]
  U3 = POT [part_number="AMP78   POS.4  POT10KLINEAR" package=pot_alpha_rv16af-20]
  U4 = POT [part_number="AMP79 (POS.5) POT 10K LINEAR" package=pot_alpha_rv16af-20]
  U5 = POT [part_number="MICROFONO (NIVEL ENTRADA)" package=pot_alpha_rv16af-20]
  U6 = POT [part_number="PEDAL30   POS.1 POT10KLINEAR" package=pot_alpha_rv16af-20]
  U7 = POT [part_number="AMP75   POS.1 POT10KLINEAR" package=pot_alpha_rv16af-20]
  U8 = POT [part_number="PEDAL31   POS.2 POT10KLINEAR" package=pot_alpha_rv16af-20]
  U9 = POT [part_number="PEDAL32  POS. 3 POT10KLINEAR" package=pot_alpha_rv16af-20]
  U10 = POT [part_number="PEDAL33  (POS. 4) POT10KLINEAR" package=pot_alpha_rv16af-20]
  U11 = POT [part_number="PEDAL34  (POS. 5) POT10KLINEAR" package=pot_alpha_rv16af-20]
  U12 = POT [part_number="VOLUME (NIVEL DE SALIDA)" package=pot_alpha_rv16af-20]
  WeMos_D1_Mini_OLED_Shield1 = WeMos D1 Mini OLED Shield [part_number="SSD1306 4PIN I2C 128X32 SCREEN"]
  U13 = 74HC4051 [package=so16]  # not connected
  Atmega1284P1 = ATmega1284P [package=pdpi]
  XTAL1 = Crystal [frequency="16 Mhz" package=THT]
  C1 = Capacitor [part_number=22pf package=cap-pth-small2]
  R1 = Resistor [tolerance=±10% resistance=10k package="1206 [SMD]"]
  C2 = Capacitor [part_number=22pf package=cap-pth-small2]
  C3 = Capacitor Polarized [package=cpol-radial-10uf-25v]
  C4 = Ceramic Capacitor [capacitance=100nF voltage=16V package="100 mil [THT, multilayer]"]
  Componente1 = FTDI Basic Programmer
  M1 = RioRand LM2596
  Componente2 = PowerBoost 500 Charger  # not connected
  U14 = LIPO-2000mAh [package=lipo-2000]  # not connected
  U15 = SWITCH-SPST-2 [package=switch-spst-vertical]
  Componente3 = Thumb Joystick [part_number="ANALOG JOYSTICK"]
  R2 = Resistor [tolerance=±10% resistance=10k package="1206 [SMD]"]
  R3 = Resistor [tolerance=±10% resistance=10k package="1206 [SMD]"]
  S1 = Pushbutton [package="[THT]"]
  Componente4 = Bluetooth HC-05 Macho
  R4 = Resistor [tolerance=±5% resistance=220 package="2010 [SMD]"]
  LED1 = smd LED [color="Red (633nm)" package="0603 [SMD]"]
  R5 = Resistor [tolerance=±5% resistance=220 package="2010 [SMD]"]
  LED2 = smd LED [color="Red (633nm)" package="0603 [SMD]"]
  LED3 = smd LED [color="Red (633nm)" package="0603 [SMD]"]
  R6 = Resistor [tolerance=±5% resistance=220 package="2010 [SMD]"]
  Componente5 = Adafruit 1.3in 240x240 IPS TFT [part_number="ILI 9341 LCD screen "]  # not connected

nets:
  N1: U1.A, U2.A, U3.A, U4.A, U5.A, U6.A, U7.A, U8.A, U9.A, U10.A, U11.A, U12.A, Componente4.VCC, R6.Pin_0
  N2: U1.E, U2.E, U3.E, U4.E, U5.E, U6.E, U7.E, U8.E, U9.E, U10.E, U11.E, U12.E, Atmega1284P1.GND#10, C1.2, R3.Pin_0, Componente4.GND, LED1.cathode, LED3.cathode
  N3: U4.S, Atmega1284P1.PA2
  N4: U5.S, Atmega1284P1.PA7
  N5: U11.S, Atmega1284P1.PA3
  N6: U12.S, Atmega1284P1.PA1
  GND: WeMos_D1_Mini_OLED_Shield1.D2, Atmega1284P1.GND#30, C2.1, C3.-, Componente1.GND, M1.Pin_4, Componente3.GND, LED2.cathode
  VCC: WeMos_D1_Mini_OLED_Shield1.D4, Atmega1284P1.VCC, Atmega1284P1.AVCC, R1.Pin_1, C3.+, Componente1.POWER, M1.Pin_3, Componente3.VCC
  N7: WeMos_D1_Mini_OLED_Shield1.RX, Atmega1284P1.PC1
  N8: WeMos_D1_Mini_OLED_Shield1.TX, Atmega1284P1.PC0
  N9: Atmega1284P1.PB2, R5.Pin_1
  N10: Atmega1284P1.RESET, R1.Pin_0, C4.1
  N11: Atmega1284P1.XTAL2, XTAL1.pin_0, C2.2
  N12: Atmega1284P1.XTAL1, XTAL1.pin_1, C1.1
  N13: Atmega1284P1.PD0, Componente1.TXO
  N14: Atmega1284P1.PD1, Componente1.RXI, Componente4.TXD
  N15: Atmega1284P1.PD2, R3.Pin_1, S1.Pin_1, S1.Pin_2
  N16: Atmega1284P1.PA6, Componente3.HORZ
  N17: Atmega1284P1.PA5, Componente3.VERT
  N18: Atmega1284P1.PA4, R2.Pin_0
  N19: C4.0, Componente1.DTR
  N20: M1.Pin_1, U15.P, R2.Pin_1
  N21: Componente4.State, R4.Pin_0

notes:
  Pots Pedales. Linear. 10K. (Bancos 1 - 9)
  Pots
  Amplificadores.
  Linear
  10k.
  (Bancos 1- 9)
  POT Nº1. Pedales.Cable azul. 30/35/40/45/50/55/60/65/70.
  CONEXION:
  VCC/GND/A7(MUX)
  POT Nº2. Pedales.Cable Cian. 31/36/41/46/51/56/61/66/71.
  CONEXION:
  VCC/GND/A5(MUX)
  POT Nº3.Pedales.Cable Ocre.
  32/37/42/47/52/57/62/67/72.
  CONEXION:
  VCC/GND/A3(MUX)
  POT Nº4.Pedales.Cable rosa.
  33/38/43/48/53/58/63/68/73.
  CONEXION:
  VCC/GND/A1(MUX)
  POT Nº5.Pedales.Cable verde.
  34/39/44/49/54/59/64/69/74.
  CONEXION:
  VCC/GND/A3(ATMEL1284).
  POTNº1 Amplifica.
  (Cable Ocre) 75/80/85/ 90/95/100/ 105/110/ 115.
  CONEXION:
  VCC/GND/A6(MUX)
  POTNº2 Amplifica.
  (Cable
  Naranja) 76/81/86/ 91/96/101/ 106/111/ 116.
  CONEXION:
  VCC/GND/A4(MUX)
  POTNº3 Amplifica.
  (Cable Amarillo) 77/82/87/92/97/102/ 107/112/117.
  CONEXION:
  VCC/GND/A2(MUX)
  POTNº4Amplifica
  (Cable Marron) 78/83/88/93/98/103/ 108/113/118.
  CONEXION:
  VCC/GND/A0(MUX)
  POTNº5Amplific
  (Cable Blanco) 79/84/89/94/99/104/ 109/114/119.
  CONEXION:
  VCC/GND/A2(Atmel1284).
  Pot Volume
  Nivel salida
  CONEXION:
  VCC/GND/A1(Atmel)
  Pot Mic
  Nivel entrada
  CONEXION:
  VCC/GND/A7(Atmel)
  PANTALLA SSD1306 4PIN . I2C. 128X32.
  Conexiones:VCC/GND/
  Pin17 SCL (Atmel)
  Cable gris /
  Pin16 SDA (Atmel)
  Cable Gris.
  Joystick Analogico
  (Solo 4 pines ya que el botón del joystick no lo vamos a utilizar).
  Conexiones:VCC/GND/
  Pin A5 (Atme)l,
  Cable marron )/
  Pin A6 (Atmel)
  Cable Ocre.
  Led de Estado conexion Bluetooth.
  Encendido cuando hay una conexion Bluetooth establecida.
  Resistencia 220 ohms.
  Conexion:GND/
  Pin STATE (HC-05)
  Modulo de conexión Bluetooth HC-05.
  AT ROLE=0 (Slave)
  115200 BAUDIOS
  CMODE=1
  Configurar para linkar con otro modulo master (mirar las mac)
  Conexión.VCC/GND/
  Pin TX (Atmel)
  Modulo de Bateria
  TP-4056.
  4 pines.
  Conexiónes.
  B+/B-= Bateria+/-.
  OUT+=Interruptor.
  OUT-=BoosterMT3608.
  Utlizar el puerto micro- usb para cargar la bateria
  Modulo Programación
  FTDI-USB.
  Conexión a traves del USB al PC para subir codigo al chip Atmel 1284.
  Posibilidad de posicionar el jumper 3,3/5 Voltios.
  3,3V para configurar los modulos HC-05.
  5V para subir codigo al chip.
  Con 5 pines de conexión
  VCC/GND/TX/RX y el pin DTR que lleva un condensador de 100 nf y se conecta al pin RESET (Atmel).
  (los pines tx y rx van al tx y rx del atmel)
  Led de Actividad MIDI.
  Se enciende cuando hay actividad MIDI.
  El anodo lleva Resistencia de 220 ohms y al pin 3 (atmel).
  La otra patilla (catodo)a GND.
  Cable morado que sale del IN+ del booster, pasa por Resistencia de 10kohms y va al pin A4 (Atmel)
  BOOSTER MT3608.
  Ajustar el tornillo hasta que baje de los 20voltios a los 5 voltios (realizar la lectura en OUT+ y OUT-)
  (Antes de conectar el circuito o el chip)
  Bateria 3-5 Voltios
  Interruptor ON/OFF
  Para apagar/encender el dispositivo.
  Boton Reset -Bancos.
  Pulsar para volver a la posicion 1 en los bancos de pedales/amplificadores.
  Led de encendido.
  Cuando el dispositivo este encendido

custom parts:
  ATmega1284P: AVR 8-bit microcontroller.
  Adafruit 1.3in 240x240 IPS TFT: We've been looking for a display like this for a long time - it's so small only 1.3" diagonal but has a high density 260 ppi, 240x240 pixel display with full-angle viewing. It looks a lot like our 1.44" 128x128 display, but has 4x as many pixels and looks great at any angle. We've seen displays of this caliber used in smartwatches and small electronic devices but they've always been MIPI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
