# Fritzing sketch Receptor USB-MIDI.Synaptic (saved by Fritzing 0.9.6b)
breadboards: 5

parts:
  Componente4 = Bluetooth HC-05 Macho
  R4 = Resistor [tolerance=±5% resistance=220 package="2010 [SMD]"]
  LED1 = smd LED [color="Red (633nm)" package="0603 [SMD]"]
  LED3 = smd LED [color="Red (633nm)" package="0603 [SMD]"]
  R6 = Resistor [tolerance=±5% resistance=220 package="2010 [SMD]"]
  U17 = PIC18F2550 [package=dil28-3]
  XTAL1 = Crystal [frequency="16 Mhz" package=THT]
  C1 = Capacitor [part_number=22pf package=cap-pth-small2]
  C2 = Capacitor [part_number=22pf package=cap-pth-small2]
  C5 = Ceramic Capacitor [capacitance=0.47µF voltage=16V package="100 mil [THT, multilayer]"]
  C6 = Ceramic Capacitor [capacitance=100nF voltage=16V package="100 mil [THT, multilayer]"]
  R7 = Resistor [tolerance=±5% resistance=4.7k package="1206 [SMD]"]
  C7 = Ceramic Capacitor [capacitance=100nF voltage=16V package="100 mil [THT, multilayer]"]
  C8 = Electrolytic Capacitor [capacitance=1µF voltage=35V package="1010 [SMD, electrolytic]"]
  D1 = Diode [package=diode-1n4148]
  D2 = Diode [package=diode-1n4148]
  Componente5 = Bluetooth HC-05 Macho
  R8 = Resistor [tolerance=±5% resistance=220 package="2010 [SMD]"]
  LED4 = smd LED [color="Red (633nm)" package="0603 [SMD]"]
  R9 = Resistor [tolerance=±5% resistance=1k package="1206 [SMD]"]
  U18 = SWITCH-SPST-2 [package=switch-spst-vertical]
  U19 = SWITCH-SPST-2 [package=switch-spst-vertical]
  USBTTL1 = USB TTL Serial Cable

nets:
  N1: Componente4.State, R4.Pin_0
  N2: Componente4.TXD, D2.C
  N3: Componente4.VCC, U18.P
  GND: Componente4.GND, LED1.cathode, LED3.cathode, C5.1, C7.1, C8.-, Componente5.GND, LED4.cathode
  VDD: R6.Pin_0, U17.VDD, C6.0, R7.Pin_0, C7.0, C8.+, R9.Pin_1, U18.O, USBTTL1.5V
  N4: U17.MCLR_VPP, R7.Pin_1
  N5: U17.VSS, XTAL1.pin_0, C2.2
  N6: U17.OSC1, XTAL1.pin_1, C1.1
  N7: U17.V-USB, C5.0
  N8: U17.RC4_D-, USBTTL1.GND
  N9: U17.RC5_D+, USBTTL1.RX
  N10: U17.RX_RC7, D1.A, D2.A, R9.Pin_0
  N11: D1.C, Componente5.TXD
  N12: Componente5.State, R8.Pin_0
  N13: Componente5.VCC, U19.P

notes:
  Led de Estado de la conexion Bluetooth.
  Encendido cuando hay una conexion Bluetooth establecida.
  Resistencia 220 ohms.
  Conexion:GND/
  Pin STATE (HC-05)
  Modulo de conexión Bluetooth HC-05.
  MASTER
  AT ROLE=1 (MASTER)
  115200 BAUDIOS
  Hay que configurarlo mediante comandos en el monitor serie del arduino IDE (pc). Para que linkee con otro modulo SLAVE (hay que mirar las MAC del MASTER y el SLAVE para poder linkarlos)
  Conexión.VCC/GND/
  Pin RX (PIC)
  Led de encendido.
  Cuando el dispositivo este encendido
  Cristal de cuarzo de 16 mhz necesario para el PIC18F-2550, lleva dos condensadores de 22 picofaradios conectados a GND
  Condensador de 0.47 microfaradios/470 nanofaradios.
  Conexion:Pin14 PIC y la otra patilla va a GND
  Condensador o capacitor de 100 nf.
  Conexion a PIN 20 PIC (PIN VCC del PIC) y tambien a R4K7 (la resistencia que está despues del pin 1 del PIC)
  y la otra patilla a GND.
  Condensador o capacitor de 100 nf.
  Conexion a PIN 20 PIC (PIN VCC del PIC) y PIN Nº1 de la salida USB (pin VCC Nº1 del USB) y tambien va a un condensador electrolitico y la otra patilla a GND.
  -------------------------------------------------------------------------------
  Condensador electrolitico de 1 microfaradio.
  Conexion a capacitor de 100 nf y la otra patilla a GND.
  PUERTO CONECTOR USB
  Utilizar un conector USB Macho para conectar al pc.
  -Cable negro es el PIN 4 del conector usb.GND.
  -Cable morado es el PIN 3 del conector usb. D+.
  -Cable verde es el PIN 2 del conector usb. D-.
  -y por ultimo, el cable naranja es el PIN 1 del conector usb. VCC
  PUERTO ICSP
  Cabel naranja pin 6.
  Cable marron pin 1.
  Diodos Zener 1N4148.
  Poner un diodo por cada dispositivo bluetooth HC-05 MASTER.
  Conexion al PIN RX del PIC (que está alimentado con 5 voltios)
  Resistencia de 1kilohmio para alimentar con 5V el pin RX del PIC
  Modulo de conexión Bluetooth HC-05.
  MASTER
  Dependiendo el firmware del modulo funcionaran unos comandos y otros no.
  Cuidado con los new version olos modulos que no pueden ser configurados como MASTER.
  AT+ROLE=1 (MASTER)
  A+ ROLE=0 (SLAVE)
  Escribir el comando AT+ROLE?
  Para verificar si el modulo esta configurado como MASTER=1 o SLAVE=0
  Escribir el comando AT+NAME? para cambiar el nombre del modulo. ejemplo AT+NAME=MANOLIN
  Escribir el comando AT+PSWD? para cambiar el password de conexion (PIN). ejemplo AT+PSWD=4689
  Escribir el comando:
  AT+UART=115200,0,0
  Para cambiar la comunicación del modulo a 115200 BAUDIOS.
  Escribir el comando
  AT+ADDR?
  Para averiguar la MAC del modulo, escribirla y ponerla despues en el modulo SLAVE.(utilizar AT+BIND para meter la MAC del modulo)
  El modulo se configuro mediante comandos en el monitor serie del arduino IDE (en el pc).Primero hay que ponerlo en modo de comandos AT (Mirar tutoriales para la conexion y configuracion)
  Se puede utilizar un FTDI-USB o un Arduino UNO para la configuracion mediante comandos.
  En este caso se utiliza un FTDI-USB.(es lo mismo)
  Para que linkee con otro modulo SLAVE , primero hay que mirar las MAC del MASTER y el SLAVE escribiendo:
  AT+ADDR?
  Escribir el comando AT+BIND y meter la direccion (MAC) del otro modulo para realizar el linkeo, en este caso pondremos la dirección (MAC) del modulo SLAVE. (PONER SIEMPRE MAYUSCULAS la direccion (MAC))
  por ejemplo:
  AT+BIND=07:HJ:YU:74:TR
  Estps modulos configurados como MASTER y que están linkados con el SLAVE, da igual como se ponga el AT+CMODE, podeis ponerlo en 1 o en 0.
  En el SLAVE linka mejor con el CMODE=1
  En el SLAVE escribir el comando
  AT+CMODE=1
  La conexion del modulo:
  VCC/GND/Pin RX (PIC)
  Interruptor 2 pines ON/OFF. Para apagar o encender cada modulo bluetooth, cuando el dispositivo este conectado al pc a traves del conector usb.
  R4K7 (4,7K)
  USB MACHO
  PIN 1 VCC
  PIN2 D-
  PIN3 D+
  PIN4 GND
